// Logisim project ALU.circ as structural Verilog: 3 circuits, main circuit main
// ALU_op_lsb
module main (
  input  [31:0] op1,
  input  [31:0] op2,
  input  [5:0] ALU_opcode,
  input  [4:0] shift_amt,
  output [31:0] ALU_res,
  output zero_flag,
  output overflow_flag,
  output carry_out
);

  wire add_flag_1_c, add_flag_1_v, comparator_1_lt, comparator_2_lt, multiplexer_5_out, sub_flag_1_c,
       sub_flag_1_v;
  wire [31:0] add, and_out, bw1, bw2, div_hi, div_lo, lui, mult_hi, mult_lo, nor_1_out, or_out,
       shifter_2_out, shifter_3_out, shifter_5_out, shifter_6_out, sll, sllv, slt, sr_, sr_v, sub, xor_1_out;

  Shifter #(.width(32)) shifter_1 (.in(op1), .\dist (shift_amt), .out(sll));
  Shifter #(.width(32), .shift("lr")) shifter_2 (.in(op1), .\dist (shift_amt), .out(shifter_2_out));
  Multiplexer #(.width(32), .enable("false")) multiplexer_1 (
    .in0(shifter_2_out), .in1(shifter_3_out), .out(sr_), .sel(ALU_opcode[0]));
  Shifter #(.width(32), .shift("ar")) shifter_3 (.in(op1), .\dist (shift_amt), .out(shifter_3_out));
  Shifter #(.width(32)) shifter_4 (.in(op1), .\dist (op2[4:0]), .out(sllv));
  Shifter #(.width(32), .shift("lr")) shifter_5 (.in(op1), .\dist (op2[4:0]), .out(shifter_5_out));
  Multiplexer #(.width(32), .enable("false")) multiplexer_2 (
    .in0(shifter_5_out), .in1(shifter_6_out), .out(sr_v), .sel(ALU_opcode[0]));
  Shifter #(.width(32), .shift("ar")) shifter_6 (.in(op1), .\dist (op2[4:0]), .out(shifter_6_out));
  Multiplier #(.width(32)) multiplier_1 (.a(op1), .b(op2), .out(mult_lo), .cout(mult_hi));  // open: cin
  Divider #(.width(32)) divider_1 (.a(op1), .b(op2), .out(div_lo), .rem(div_hi));  // open: upper
  add_flag add_flag_1 (.op1(op1), .op2(op2), .res(add), .v(add_flag_1_v), .c(add_flag_1_c));
  sub_flag sub_flag_1 (.op1(op1), .op2(op2), .res(sub), .v(sub_flag_1_v), .c(sub_flag_1_c));
  assign and_out = op1 & op2;  // AND_Gate and, 32 bits wide
  Multiplexer #(.width(32), .enable("false")) multiplexer_3 (
    .in0(and_out), .in1(or_out), .out(bw1), .sel(ALU_opcode[0]));
  assign or_out = op1 | op2;  // OR_Gate or, 32 bits wide
  assign xor_1_out = op1 ^ op2;  // XOR_Gate xor_1, 32 bits wide
  Multiplexer #(.width(32), .enable("false")) multiplexer_4 (
    .in0(xor_1_out), .in1(nor_1_out), .out(bw2), .sel(ALU_opcode[0]));
  assign nor_1_out = ~(op1 | op2);  // NOR_Gate nor_1, 32 bits wide
  Shifter #(.width(32)) shifter_7 (.in(op2), .\dist (5'b10000), .out(lui));
  Comparator #(.width(32)) comparator_1 (.a(op1), .b(op2), .lt(comparator_1_lt));  // open: gt, eq
  Multiplexer #(.enable("false")) multiplexer_5 (
    .in0(comparator_1_lt), .in1(comparator_2_lt), .out(multiplexer_5_out), .sel(ALU_opcode[0]));
  Comparator #(.width(32), .mode("unsigned")) comparator_2 (.a(op1), .b(op2), .lt(comparator_2_lt));  // open: gt, eq
  assign slt = {{31{1'b0}}, multiplexer_5_out};  // Bit_Extender bit_extender_1
  Multiplexer #(.select(5), .width(32), .enable("false")) multiplexer_6 (
    .in0(sll), .in1(sr_), .in2(sllv), .in3(sr_v), .in4(op1), .in16(add), .in17(sub), .in18(bw1), .in19(bw2),
    .in20(lui), .in21(slt), .out(ALU_res), .sel(ALU_opcode[5:1]));  // open: in5, in6, in7, in8, in9, in10, in11, in12, in13, in14, in15, in22, in23, in24, in25, in26, in27, in28, in29, in30, in31

  // Other names for the same wires on the sheet: ALU_op[5:0] = ALU_opcode; ALUop_lsb = ALU_opcode[0];
  //   op_shamt[4:0] = op2[4:0]; shamt[4:0] = shift_amt
endmodule

module add_flag (
  input  [31:0] op1,
  input  [31:0] op2,
  output [31:0] res,
  output v,
  output c
);

  wire xor_1_out, xor_2_out;

  Adder #(.width(32)) adder_1 (.a(op1), .b(op2), .out(res), .cin(1'b0), .cout(c));
  xor xor_1 (xor_1_out, op1[31], res[31]);
  xor xor_2 (xor_2_out, res[31], op2[31]);
  and and_1 (v, xor_1_out, xor_2_out);

  // Other names for the same wires on the sheet: cout_flag = c; overflow_flag = v
endmodule

module sub_flag (
  input  [31:0] op1,
  input  [31:0] op2,
  output [31:0] res,
  output v,
  output c
);

  wire xor_1_out, xor_2_out;

  Subtractor #(.width(32)) subtractor_1 (.a(op1), .b(op2), .out(res), .bin(1'b0), .bout(c));
  xor xor_1 (xor_1_out, op1[31], res[31]);
  xor xor_2 (xor_2_out, res[31], ~op2[31]);  // XOR_Gate
  and and_1 (v, xor_1_out, xor_2_out);

  // Other names for the same wires on the sheet: cout_flag = c; overflow_flag = v
endmodule
